// Logisim project ALU.circ as structural Verilog: 1 circuit, main circuit main
module main (
  input  [15:0] in_1,
  input  nx,
  input  zx,
  input  no,
  input  [15:0] in_5,
  input  f,
  input  ny,
  input  zy,
  output [15:0] out_9,
  output [15:0] out_10,
  output [15:0] out_11,
  output [15:0] out_12,
  output [15:0] out_13,
  output [15:0] out_14,
  output ng,
  output zr
);

  wire or_1_out;
  wire [15:0] adder_1_out, adder_2_out, adder_3_out, and_1_out, multiplexer_1_out, multiplexer_2_out,
       not_1_out, not_2_out, not_3_out, not_4_out, not_5_out, not_6_out, not_7_out;

  assign not_1_out = ~in_1;  // NOT_Gate not_1, 16 bits wide
  assign not_2_out = ~in_5;  // NOT_Gate not_2, 16 bits wide
  Adder #(.width(16)) adder_1 (.a(in_1), .b(not_1_out), .out(adder_1_out));  // open: cin, cout
  Adder #(.width(16)) adder_2 (.a(in_5), .b(not_2_out), .out(adder_2_out));  // open: cin, cout
  Multiplexer #(.width(16), .enable("false")) multiplexer_1 (
    .in0(in_1), .in1(adder_1_out), .out(multiplexer_1_out), .sel(zx));
  Multiplexer #(.width(16), .enable("false")) multiplexer_2 (
    .in0(in_5), .in1(adder_2_out), .out(multiplexer_2_out), .sel(zy));
  assign not_3_out = ~multiplexer_1_out;  // NOT_Gate not_3, 16 bits wide
  assign not_4_out = ~multiplexer_2_out;  // NOT_Gate not_4, 16 bits wide
  Multiplexer #(.width(16), .enable("false")) multiplexer_3 (
    .in0(multiplexer_1_out), .in1(not_3_out), .out(out_11), .sel(zx));
  Multiplexer #(.width(16), .enable("false")) multiplexer_4 (
    .in0(multiplexer_2_out), .in1(not_4_out), .out(out_14), .sel(zy));
  Multiplexer #(.width(16), .enable("false")) multiplexer_5 (.in0(out_11), .in1(not_5_out), .out(out_10), .sel(nx));
  assign not_5_out = ~out_11;  // NOT_Gate not_5, 16 bits wide
  Multiplexer #(.width(16), .enable("false")) multiplexer_6 (.in0(out_14), .in1(not_6_out), .out(out_13), .sel(ny));
  assign not_6_out = ~out_14;  // NOT_Gate not_6, 16 bits wide
  assign and_1_out = out_10 & out_13;  // AND_Gate and_1, 16 bits wide
  Adder #(.width(16)) adder_3 (.a(out_10), .b(out_13), .out(adder_3_out));  // open: cin, cout
  Multiplexer #(.width(16), .enable("false")) multiplexer_7 (.in0(and_1_out), .in1(adder_3_out), .out(out_12), .sel(f));
  Multiplexer #(.width(16), .enable("false")) multiplexer_8 (
    .in0(out_12), .in1(not_7_out), .out({ng, out_9[14:0]}), .sel(no));
  assign not_7_out = ~out_12;  // NOT_Gate not_7, 16 bits wide
  not not_8 (zr, or_1_out);
  or or_1 (or_1_out, out_9[0], out_9[1], out_9[2], out_9[3], out_9[4], out_9[5], out_9[6], out_9[7], out_9[8], out_9[9], out_9[10], out_9[11], out_9[12], out_9[13], out_9[14], ng);
  _7_Segment_Display u_7_segment_display_1 (
    .f(or_1_out), .a(or_1_out), .b(or_1_out), .e(or_1_out), .d(or_1_out), .c(or_1_out));  // open: g, dp
  _7_Segment_Display u_7_segment_display_2 (.f(or_1_out), .e(or_1_out), .d(or_1_out));  // open: g, a, b, c, dp
  _7_Segment_Display u_7_segment_display_3 (.f(or_1_out), .e(or_1_out), .d(or_1_out));  // open: g, a, b, c, dp

  assign out_9[15] = ng;

  // Notes on the sheet:
  //   x
  //   y
  //   I promise
  //   seriously this is mine I didn't steal this from anyone
  //   ALU Built by Markyan
  //   girugamesh
  //   weeaboo
  //   out
endmodule
