// Logisim project BCDto7digitDisplay.circ as structural Verilog: 1 circuit, main circuit main
module main (
  input  in_1,
  input  in_2,
  input  in_3,
  input  in_4
);

  wire _1, _2, _4, _8, a, and_1_out, and_2_out, and_3_out, and_4_out, and_5_out, and_6_out, and_7_out,
       and_8_out, and_9_out, and_10_out, and_11_out, and_12_out, and_13_out, b, button_1_out, c, clock_1_out,
       clock_2_out, d, Dot, e, f, g, not_1_out, not_2_out, not_3_out, not_4_out;
  wire [7:0] counter_2_q;
  wire [9:0] counter_1_q;

  Clock clock_1 (.out(clock_1_out));
  not not_1 (not_1_out, in_1);
  Button button_1 (.out(button_1_out));
  and and_1 (and_1_out, clock_1_out, in_4);
  Clock clock_2 (.out(clock_2_out));
  and and_2 (and_2_out, in_1, clock_2_out);
  and and_3 (and_3_out, not_1_out, button_1_out);
  LED led_1 (.in(_4));
  LED led_2 (.in(_8));
  LED led_3 (.in(_2));
  LED led_4 (.in(counter_1_q[7]));
  LED led_5 (.in(counter_1_q[8]));
  LED led_6 (.in(counter_1_q[9]));
  LED led_7 (.in(counter_1_q[6]));
  Counter #(.width(10), .max('h3ff)) counter_1 (
    .load(in_3), .Q(counter_1_q), .clk(and_1_out));  // open: D, count, carry, clr
  Counter #(.max('h9)) counter_2 (.load(in_2), .Q(counter_2_q), .clk(Dot), .clr(and_4_out));  // open: D, count, carry
  or or_1 (Dot, and_2_out, and_3_out);
  and and_4 (and_4_out, _8, _4);
  LED led_8 (.in(_1));
  LED led_9 (.in(counter_1_q[3]));
  LED led_10 (.in(counter_1_q[4]));
  LED led_11 (.in(counter_1_q[2]));
  LED led_12 (.in(counter_1_q[5]));
  Bit_Extender #(.out_width(4)) bit_extender_1 (.in(counter_2_q), .out({_8, _4, _2, _1}));
  _7_Segment_Display u_7_segment_display_1 (.g(g), .f(f), .a(a), .b(b), .e(e), .d(d), .c(c), .dp(Dot));
  LED led_13 (.in(counter_1_q[0]));
  LED led_14 (.in(counter_1_q[1]));
  not not_2 (not_2_out, _1);
  not not_3 (not_3_out, _2);
  not not_4 (not_4_out, _4);
  and and_5 (and_5_out, _1, _2);
  and and_6 (and_6_out, _1, _4);
  and and_7 (and_7_out, not_2_out, not_3_out);
  and and_8 (and_8_out, not_2_out, not_4_out);
  and and_9 (and_9_out, not_2_out, _2);
  and and_10 (and_10_out, _2, not_4_out);
  and and_11 (and_11_out, not_2_out, _4);
  and and_12 (and_12_out, not_3_out, _4);
  and and_13 (and_13_out, _1, not_3_out, _4);
  or or_2 (a, and_5_out, and_6_out, and_9_out, and_8_out, _8);
  or or_3 (b, and_5_out, and_7_out, not_4_out);
  or or_4 (c, _1, not_3_out, _4);
  or or_5 (d, and_8_out, and_9_out, _8, and_10_out, and_13_out);
  or or_6 (e, and_8_out, and_9_out);
  or or_7 (f, and_7_out, and_12_out, and_11_out, _8);
  or or_8 (g, and_9_out, and_10_out, and_12_out, _8);

  // Notes on the sheet:
  //   a
  //   b
  //   c
  //   d
  //   e
  //   f
  //   g
endmodule
