// Logisim project CPU.circ as structural Verilog
module main (
  input  [15:0] instruction,
  input  [15:0] inM,
  input  Reset,
  input  Clock,
  output writeM,
  output [15:0] out,
  output [15:0] addressM,
  output [15:0] pc
);

  wire decoder_1_a, decoder_1_i, inc, load, ng, storer_1_loadareg, storer_1_loaddreg, zr;
  wire [2:0] decoder_1_d, decoder_1_j;
  wire [5:0] decoder_1_c;
  wire [15:0] d_register_1_out, multiplexer_1_out, multiplexer_2_out;

  Multiplexer #(.width(16), .enable("false")) multiplexer_1 (
    .in0(instruction), .in1(out), .out(multiplexer_1_out), .sel(decoder_1_i));
  A_Register a_register_1 (.in(multiplexer_1_out), .out(addressM), .clock(Clock), .load(storer_1_loadareg));
  Decoder decoder_1 (
    .in_1(instruction), .i(decoder_1_i), .a(decoder_1_a), .c(decoder_1_c), .d(decoder_1_d), .j(decoder_1_j));  // open: A_instruction
  D_Register d_register_1 (.in(out), .out(d_register_1_out), .clock(Clock), .load(storer_1_loaddreg));
  Multiplexer #(.width(16), .enable("false")) multiplexer_2 (
    .in0(addressM), .in1(inM), .out(multiplexer_2_out), .sel(decoder_1_a));
  Storer storer_1 (
    .LoadMreg(writeM), .LoadDreg(storer_1_loaddreg), .LoadAreg(storer_1_loadareg), .i(decoder_1_i),
    .j3(decoder_1_d[2]), .j2(decoder_1_d[1]), .j1(decoder_1_d[0]));
  PC pc_1 (.in(addressM), .out(pc), .inc(inc), .load(load), .reset(Reset), .clock(Clock));
  ALU2 alu2_1 (
    .x(d_register_1_out), .y(multiplexer_2_out), .out(out), .zx(decoder_1_c[5]), .zy(decoder_1_c[4]),
    .nx(decoder_1_c[3]), .ny(decoder_1_c[2]), .f(decoder_1_c[1]), .no(decoder_1_c[0]), .zr(zr), .ng(ng));
  Comparer comparer_1 (.loadout(load), .j3(decoder_1_j[2]), .j2(decoder_1_j[1]), .j1(decoder_1_j[0]), .zr(zr), .ng(ng));
  not not_1 (inc, load);

  // Notes on the sheet:
  //   D
  //   A/M
endmodule

module ALU2 (
  input  zx,
  input  zy,
  input  nx,
  input  ny,
  input  f,
  input  no,
  input  [15:0] x,
  input  [15:0] y,
  output [15:0] out,
  output zr,
  output ng
);

  wire or_1_out;
  wire [15:0] adder_1_out, adder_2_out, adder_3_out, and_1_out, multiplexer_1_out, multiplexer_2_out,
       multiplexer_3_out, multiplexer_4_out, multiplexer_5_out, multiplexer_6_out, multiplexer_7_out,
       not_1_out, not_2_out, not_3_out, not_4_out, not_5_out, not_6_out, not_7_out;

  assign not_1_out = ~x;  // NOT_Gate not_1, 16 bits wide
  assign not_2_out = ~y;  // NOT_Gate not_2, 16 bits wide
  Adder #(.width(16)) adder_1 (.a(x), .b(not_1_out), .out(adder_1_out));  // open: cin, cout
  Adder #(.width(16)) adder_2 (.a(y), .b(not_2_out), .out(adder_2_out));  // open: cin, cout
  Multiplexer #(.width(16), .enable("false")) multiplexer_1 (
    .in0(x), .in1(adder_1_out), .out(multiplexer_1_out), .sel(zx));
  Multiplexer #(.width(16), .enable("false")) multiplexer_2 (
    .in0(y), .in1(adder_2_out), .out(multiplexer_2_out), .sel(zy));
  assign not_3_out = ~multiplexer_1_out;  // NOT_Gate not_3, 16 bits wide
  assign not_4_out = ~multiplexer_2_out;  // NOT_Gate not_4, 16 bits wide
  Multiplexer #(.width(16), .enable("false")) multiplexer_3 (
    .in0(multiplexer_1_out), .in1(not_3_out), .out(multiplexer_3_out), .sel(zx));
  Multiplexer #(.width(16), .enable("false")) multiplexer_4 (
    .in0(multiplexer_2_out), .in1(not_4_out), .out(multiplexer_4_out), .sel(zy));
  Multiplexer #(.width(16), .enable("false")) multiplexer_5 (
    .in0(multiplexer_3_out), .in1(not_5_out), .out(multiplexer_5_out), .sel(nx));
  assign not_5_out = ~multiplexer_3_out;  // NOT_Gate not_5, 16 bits wide
  Multiplexer #(.width(16), .enable("false")) multiplexer_6 (
    .in0(multiplexer_4_out), .in1(not_6_out), .out(multiplexer_6_out), .sel(ny));
  assign not_6_out = ~multiplexer_4_out;  // NOT_Gate not_6, 16 bits wide
  assign and_1_out = multiplexer_5_out & multiplexer_6_out;  // AND_Gate and_1, 16 bits wide
  Adder #(.width(16)) adder_3 (.a(multiplexer_5_out), .b(multiplexer_6_out), .out(adder_3_out));  // open: cin, cout
  Multiplexer #(.width(16), .enable("false")) multiplexer_7 (
    .in0(and_1_out), .in1(adder_3_out), .out(multiplexer_7_out), .sel(f));
  Multiplexer #(.width(16), .enable("false")) multiplexer_8 (
    .in0(multiplexer_7_out), .in1(not_7_out), .out({ng, out[14:0]}), .sel(no));
  assign not_7_out = ~multiplexer_7_out;  // NOT_Gate not_7, 16 bits wide
  not not_8 (zr, or_1_out);
  or or_1 (or_1_out, out[0], out[1], out[2], out[3], out[4], out[5], out[6], out[7], out[8], out[9], out[10], out[11], out[12], out[13], out[14], ng);

  assign out[15] = ng;
endmodule

module PC (
  input  inc,
  input  load,
  input  reset,
  input  [15:0] in,
  input  clock,
  output [15:0] out
);

  wire [15:0] adder_1_out, adder_2_out, multiplexer_1_out, multiplexer_2_out, multiplexer_3_out,
       multiplexer_4_out, not_1_out, not_2_out;

  Multiplexer #(.width(16), .enable("false")) multiplexer_1 (
    .in0(multiplexer_4_out), .in1(in), .out(multiplexer_1_out), .sel(load));
  assign not_1_out = ~multiplexer_1_out;  // NOT_Gate not_1, 16 bits wide
  Adder #(.width(16)) adder_1 (.a(multiplexer_1_out), .b(not_1_out), .out(adder_1_out));  // open: cin, cout
  Multiplexer #(.width(16), .enable("false")) multiplexer_2 (
    .in0(multiplexer_1_out), .in1(adder_1_out), .out(multiplexer_2_out), .sel(reset));
  assign not_2_out = ~multiplexer_2_out;  // NOT_Gate not_2, 16 bits wide
  Multiplexer #(.width(16), .enable("false")) multiplexer_3 (
    .in0(multiplexer_2_out), .in1(not_2_out), .out(multiplexer_3_out), .sel(reset));
  Register #(.width(16)) register_1 (.D(multiplexer_3_out), .Q(out), .clk(clock));  // open: en, clr
  Adder #(.width(16)) adder_2 (.a(16'h1), .b(out), .out(adder_2_out));  // open: cin, cout
  Multiplexer #(.width(16), .enable("false")) multiplexer_4 (
    .in0(out), .in1(adder_2_out), .out(multiplexer_4_out), .sel(inc));

  // Notes on the sheet:
  //   inc
endmodule

module Decoder (
  input  [15:0] in_1,
  output [15:0] A_instruction,
  output i,
  output a,
  output [5:0] c,
  output [2:0] d,
  output [2:0] j
);


  assign a = in_1[12];
  assign A_instruction = in_1;
  assign c = in_1[11:6];
  assign d = in_1[5:3];
  assign i = in_1[15];
  assign j = in_1[2:0];
endmodule

module A_Register (
  input  [15:0] in,
  input  clock,
  input  load,
  output [15:0] out
);

  wire multiplexer_1_out, multiplexer_2_out, multiplexer_3_out, multiplexer_4_out, multiplexer_5_out,
       multiplexer_6_out, multiplexer_7_out, multiplexer_8_out, multiplexer_9_out, multiplexer_10_out,
       multiplexer_11_out, multiplexer_12_out, multiplexer_13_out, multiplexer_14_out, multiplexer_15_out,
       multiplexer_16_out;

  Multiplexer #(.enable("false")) multiplexer_1 (.in0(out[0]), .in1(in[0]), .out(multiplexer_1_out), .sel(load));
  Multiplexer #(.enable("false")) multiplexer_2 (.in0(out[1]), .in1(in[1]), .out(multiplexer_2_out), .sel(load));
  Multiplexer #(.enable("false")) multiplexer_3 (.in0(out[2]), .in1(in[2]), .out(multiplexer_3_out), .sel(load));
  Multiplexer #(.enable("false")) multiplexer_4 (.in0(out[3]), .in1(in[3]), .out(multiplexer_4_out), .sel(load));
  Multiplexer #(.enable("false")) multiplexer_5 (.in0(out[4]), .in1(in[4]), .out(multiplexer_5_out), .sel(load));
  Multiplexer #(.enable("false")) multiplexer_6 (.in0(out[5]), .in1(in[5]), .out(multiplexer_6_out), .sel(load));
  Multiplexer #(.enable("false")) multiplexer_7 (.in0(out[6]), .in1(in[6]), .out(multiplexer_7_out), .sel(load));
  Multiplexer #(.enable("false")) multiplexer_8 (.in0(out[7]), .in1(in[7]), .out(multiplexer_8_out), .sel(load));
  Multiplexer #(.enable("false")) multiplexer_9 (.in0(out[8]), .in1(in[8]), .out(multiplexer_9_out), .sel(load));
  Multiplexer #(.enable("false")) multiplexer_10 (.in0(out[9]), .in1(in[9]), .out(multiplexer_10_out), .sel(load));
  Multiplexer #(.enable("false")) multiplexer_11 (.in0(out[10]), .in1(in[10]), .out(multiplexer_11_out), .sel(load));
  Multiplexer #(.enable("false")) multiplexer_12 (.in0(out[11]), .in1(in[11]), .out(multiplexer_12_out), .sel(load));
  Multiplexer #(.enable("false")) multiplexer_13 (.in0(out[12]), .in1(in[12]), .out(multiplexer_13_out), .sel(load));
  Multiplexer #(.enable("false")) multiplexer_14 (.in0(out[13]), .in1(in[13]), .out(multiplexer_14_out), .sel(load));
  Multiplexer #(.enable("false")) multiplexer_15 (.in0(out[14]), .in1(in[14]), .out(multiplexer_15_out), .sel(load));
  Multiplexer #(.enable("false")) multiplexer_16 (.in0(out[15]), .in1(in[15]), .out(multiplexer_16_out), .sel(out[15]));
  D_Flip_Flop d_ff_1 (.clk(clock), .D(multiplexer_1_out), .Q(out[0]));  // open: Qn, preset, en, reset
  D_Flip_Flop d_ff_2 (.clk(clock), .D(multiplexer_2_out), .Q(out[1]));  // open: Qn, preset, en, reset
  D_Flip_Flop d_ff_3 (.clk(clock), .D(multiplexer_3_out), .Q(out[2]));  // open: Qn, preset, en, reset
  D_Flip_Flop d_ff_4 (.clk(clock), .D(multiplexer_4_out), .Q(out[3]));  // open: Qn, preset, en, reset
  D_Flip_Flop d_ff_5 (.clk(clock), .D(multiplexer_5_out), .Q(out[4]));  // open: Qn, preset, en, reset
  D_Flip_Flop d_ff_6 (.clk(clock), .D(multiplexer_6_out), .Q(out[5]));  // open: Qn, preset, en, reset
  D_Flip_Flop d_ff_7 (.clk(clock), .D(multiplexer_7_out), .Q(out[6]));  // open: Qn, preset, en, reset
  D_Flip_Flop d_ff_8 (.clk(clock), .D(multiplexer_8_out), .Q(out[7]));  // open: Qn, preset, en, reset
  D_Flip_Flop d_ff_9 (.clk(clock), .D(multiplexer_9_out), .Q(out[8]));  // open: Qn, preset, en, reset
  D_Flip_Flop d_ff_10 (.clk(clock), .D(multiplexer_10_out), .Q(out[9]));  // open: Qn, preset, en, reset
  D_Flip_Flop d_ff_11 (.clk(clock), .D(multiplexer_11_out), .Q(out[10]));  // open: Qn, preset, en, reset
  D_Flip_Flop d_ff_12 (.clk(clock), .D(multiplexer_12_out), .Q(out[11]));  // open: Qn, preset, en, reset
  D_Flip_Flop d_ff_13 (.clk(clock), .D(multiplexer_13_out), .Q(out[12]));  // open: Qn, preset, en, reset
  D_Flip_Flop d_ff_14 (.clk(clock), .D(multiplexer_14_out), .Q(out[13]));  // open: Qn, preset, en, reset
  D_Flip_Flop d_ff_15 (.clk(clock), .D(multiplexer_15_out), .Q(out[14]));  // open: Qn, preset, en, reset
  D_Flip_Flop d_ff_16 (.clk(clock), .D(multiplexer_16_out), .Q(out[15]));  // open: Qn, preset, en, reset
endmodule

module D_Register (
  input  [15:0] in,
  input  clock,
  input  load,
  output [15:0] out
);

  wire multiplexer_1_out, multiplexer_2_out, multiplexer_3_out, multiplexer_4_out, multiplexer_5_out,
       multiplexer_6_out, multiplexer_7_out, multiplexer_8_out, multiplexer_9_out, multiplexer_10_out,
       multiplexer_11_out, multiplexer_12_out, multiplexer_13_out, multiplexer_14_out, multiplexer_15_out,
       multiplexer_16_out;

  Multiplexer #(.enable("false")) multiplexer_1 (.in0(out[0]), .in1(in[0]), .out(multiplexer_1_out), .sel(load));
  Multiplexer #(.enable("false")) multiplexer_2 (.in0(out[1]), .in1(in[1]), .out(multiplexer_2_out), .sel(load));
  Multiplexer #(.enable("false")) multiplexer_3 (.in0(out[2]), .in1(in[2]), .out(multiplexer_3_out), .sel(load));
  Multiplexer #(.enable("false")) multiplexer_4 (.in0(out[3]), .in1(in[3]), .out(multiplexer_4_out), .sel(load));
  Multiplexer #(.enable("false")) multiplexer_5 (.in0(out[4]), .in1(in[4]), .out(multiplexer_5_out), .sel(load));
  Multiplexer #(.enable("false")) multiplexer_6 (.in0(out[5]), .in1(in[5]), .out(multiplexer_6_out), .sel(load));
  Multiplexer #(.enable("false")) multiplexer_7 (.in0(out[6]), .in1(in[6]), .out(multiplexer_7_out), .sel(load));
  Multiplexer #(.enable("false")) multiplexer_8 (.in0(out[7]), .in1(in[7]), .out(multiplexer_8_out), .sel(load));
  Multiplexer #(.enable("false")) multiplexer_9 (.in0(out[8]), .in1(in[8]), .out(multiplexer_9_out), .sel(load));
  Multiplexer #(.enable("false")) multiplexer_10 (.in0(out[9]), .in1(in[9]), .out(multiplexer_10_out), .sel(load));
  Multiplexer #(.enable("false")) multiplexer_11 (.in0(out[10]), .in1(in[10]), .out(multiplexer_11_out), .sel(load));
  Multiplexer #(.enable("false")) multiplexer_12 (.in0(out[11]), .in1(in[11]), .out(multiplexer_12_out), .sel(load));
  Multiplexer #(.enable("false")) multiplexer_13 (.in0(out[12]), .in1(in[12]), .out(multiplexer_13_out), .sel(load));
  Multiplexer #(.enable("false")) multiplexer_14 (.in0(out[13]), .in1(in[13]), .out(multiplexer_14_out), .sel(load));
  Multiplexer #(.enable("false")) multiplexer_15 (.in0(out[14]), .in1(in[14]), .out(multiplexer_15_out), .sel(load));
  Multiplexer #(.enable("false")) multiplexer_16 (.in0(out[15]), .in1(in[15]), .out(multiplexer_16_out), .sel(out[15]));
  D_Flip_Flop d_ff_1 (.clk(clock), .D(multiplexer_1_out), .Q(out[0]));  // open: Qn, preset, en, reset
  D_Flip_Flop d_ff_2 (.clk(clock), .D(multiplexer_2_out), .Q(out[1]));  // open: Qn, preset, en, reset
  D_Flip_Flop d_ff_3 (.clk(clock), .D(multiplexer_3_out), .Q(out[2]));  // open: Qn, preset, en, reset
  D_Flip_Flop d_ff_4 (.clk(clock), .D(multiplexer_4_out), .Q(out[3]));  // open: Qn, preset, en, reset
  D_Flip_Flop d_ff_5 (.clk(clock), .D(multiplexer_5_out), .Q(out[4]));  // open: Qn, preset, en, reset
  D_Flip_Flop d_ff_6 (.clk(clock), .D(multiplexer_6_out), .Q(out[5]));  // open: Qn, preset, en, reset
  D_Flip_Flop d_ff_7 (.clk(clock), .D(multiplexer_7_out), .Q(out[6]));  // open: Qn, preset, en, reset
  D_Flip_Flop d_ff_8 (.clk(clock), .D(multiplexer_8_out), .Q(out[7]));  // open: Qn, preset, en, reset
  D_Flip_Flop d_ff_9 (.clk(clock), .D(multiplexer_9_out), .Q(out[8]));  // open: Qn, preset, en, reset
  D_Flip_Flop d_ff_10 (.clk(clock), .D(multiplexer_10_out), .Q(out[9]));  // open: Qn, preset, en, reset
  D_Flip_Flop d_ff_11 (.clk(clock), .D(multiplexer_11_out), .Q(out[10]));  // open: Qn, preset, en, reset
  D_Flip_Flop d_ff_12 (.clk(clock), .D(multiplexer_12_out), .Q(out[11]));  // open: Qn, preset, en, reset
  D_Flip_Flop d_ff_13 (.clk(clock), .D(multiplexer_13_out), .Q(out[12]));  // open: Qn, preset, en, reset
  D_Flip_Flop d_ff_14 (.clk(clock), .D(multiplexer_14_out), .Q(out[13]));  // open: Qn, preset, en, reset
  D_Flip_Flop d_ff_15 (.clk(clock), .D(multiplexer_15_out), .Q(out[14]));  // open: Qn, preset, en, reset
  D_Flip_Flop d_ff_16 (.clk(clock), .D(multiplexer_16_out), .Q(out[15]));  // open: Qn, preset, en, reset
endmodule

module Comparer (
  input  j3,
  input  j2,
  input  j1,
  input  zr,
  input  ng,
  output loadout
);

  wire and_1_out, and_2_out, and_3_out, not_1_out, or_1_out, or_2_out, or_4_out;

  or or_1 (or_1_out, ng, zr);
  not not_1 (not_1_out, or_1_out);
  and and_1 (and_1_out, not_1_out, j3);
  and and_2 (and_2_out, zr, j2);
  and and_3 (and_3_out, j1, ng);
  or or_2 (or_2_out, and_1_out, and_2_out);
  or or_3 (loadout, or_2_out, or_4_out);
  or or_4 (or_4_out, and_2_out, and_3_out);
endmodule

module Storer (
  input  i,
  input  j3,
  input  j2,
  input  j1,
  output LoadMreg,
  output LoadDreg,
  output LoadAreg
);

  wire and_3_out, not_1_out;

  and and_1 (LoadMreg, i, j1);
  and and_2 (LoadDreg, i, j2);
  and and_3 (and_3_out, i, j3);
  not not_1 (not_1_out, i);
  or or_1 (LoadAreg, and_3_out, not_1_out);
endmodule
