// Logisim project EasyPC.circ as structural Verilog: 1 circuit, main circuit main
module main (
  input  load,
  input  inc,
  input  reset,
  input  [15:0] in_4,
  output [15:0] out_5,
  output [15:0] out_6
);

  wire clock_1_out;
  wire [15:0] adder_1_out, multiplexer_1_out;

  Multiplexer #(.select(3), .width(16), .enable("false")) multiplexer_1 (
    .in1({16{1'b0}}), .in2(adder_1_out), .in4(in_4), .in6(in_4), .out(multiplexer_1_out),
    .sel({load, inc, reset}));  // open: in0, in3, in5, in7
  Clock clock_1 (.out(clock_1_out));
  Register #(.width(16)) register_1 (.D(multiplexer_1_out), .Q(out_5), .clk(clock_1_out));  // open: en, clr
  Adder #(.width(16)) adder_1 (.a(out_5), .b(16'h1), .out(adder_1_out));  // open: cin, cout
endmodule
