// Logisim project MoarCircuits.circ as structural Verilog: 1 circuit, main circuit main
module main (
  input  in_1,
  input  in_2,
  input  in_3,
  input  in_4,
  input  in_5,
  input  in_6,
  input  in_7,
  input  in_8,
  input  in_9,
  input  in_10,
  input  sel,
  input  in_12,
  input  b,
  input  a,
  input  in_15,
  input  sel_2,
  input  in_17,
  input  in_18,
  input  in,
  output And,
  output out_21,
  output Or,
  output out_23,
  output Not,
  output Xor,
  output out_26,
  output Mux,
  output dogg,
  output snoop
);

  wire and_1_out, and_2_out, and_3_out, and_4_out, and_5_out, nand_1_out, nand_2_out, nand_3_out, nand_5_out,
       nand_6_out, nand_7_out, nand_10_out, nand_11_out, nand_12_out, nand_13_out, nand_14_out, nand_15_out,
       nand_16_out, nand_17_out, nand_18_out, nand_19_out, nand_20_out, nand_21_out, nand_22_out, not_1_out,
       not_2_out, not_3_out, not_4_out;

  not not_1 (not_1_out, in_9);
  not not_2 (not_2_out, in_6);
  not not_3 (not_3_out, sel);
  not not_4 (not_4_out, sel_2);
  and and_1 (and_1_out, in_1, in_4);
  not not_5 (out_21, and_1_out);
  and and_2 (and_2_out, in_6, not_1_out);
  and and_3 (and_3_out, not_2_out, in_9);
  and and_4 (and_4_out, sel, b);
  and and_5 (and_5_out, not_3_out, a);
  and and_6 (dogg, in, sel_2);
  and and_7 (snoop, in, not_4_out);
  or or_1 (out_23, and_2_out, and_3_out);
  or or_2 (out_26, and_4_out, and_5_out);
  nand nand_1 (nand_1_out, in_2, in_3);
  nand nand_2 (nand_2_out, in_5, in_5);
  nand nand_3 (nand_3_out, in_7, in_7);
  nand nand_4 (Not, in_8, in_8);
  nand nand_5 (nand_5_out, in_12, in_12);
  nand nand_6 (nand_6_out, in_10, in_10);
  nand nand_7 (nand_7_out, in_15, in_15);
  nand nand_8 (And, nand_1_out, nand_1_out);
  nand nand_9 (Or, nand_2_out, nand_3_out);
  nand nand_10 (nand_10_out, in_10, nand_5_out);
  nand nand_11 (nand_11_out, nand_6_out, in_12);
  nand nand_12 (nand_12_out, nand_7_out, nand_7_out);
  nand nand_13 (nand_13_out, nand_12_out, in_17);
  nand nand_14 (nand_14_out, nand_7_out, in_18);
  nand nand_15 (nand_15_out, nand_10_out, nand_10_out);
  nand nand_16 (nand_16_out, nand_11_out, nand_11_out);
  nand nand_17 (nand_17_out, nand_13_out, nand_13_out);
  nand nand_18 (nand_18_out, nand_14_out, nand_14_out);
  nand nand_19 (nand_19_out, nand_15_out, nand_15_out);
  nand nand_20 (nand_20_out, nand_16_out, nand_16_out);
  nand nand_21 (nand_21_out, nand_17_out, nand_17_out);
  nand nand_22 (nand_22_out, nand_18_out, nand_18_out);
  nand nand_23 (Mux, nand_21_out, nand_22_out);
  nand nand_24 (Xor, nand_19_out, nand_20_out);

  // Notes on the sheet:
  //   Mux
  //   NAND
  //   XOR
endmodule
