// Logisim project MoarCircuits2.circ as structural Verilog: 1 circuit, main circuit main
module main (
  input  [15:0] in_1,
  input  [15:0] in_2,
  input  in_3,
  input  [15:0] in_4,
  input  in_5,
  input  in_6,
  input  [15:0] in_7,
  input  in_8,
  input  in_9,
  input  in_10,
  input  [15:0] in_11,
  input  [15:0] in_12,
  input  in_13,
  input  in_14,
  input  [15:0] in_15,
  input  in_16,
  input  [15:0] in_17,
  input  [15:0] in_18,
  input  [15:0] in_19,
  input  [15:0] in_20,
  input  [15:0] in_21,
  input  in_22,
  input  in_23,
  input  in_24,
  output out_25,
  output out_26,
  output [15:0] out_27,
  output out_28,
  output out_29,
  output out_30,
  output out_31,
  output out_32,
  output out_33,
  output out_34,
  output out_35,
  output out_36,
  output out_37,
  output [15:0] out_38
);

  wire demultiplexer_1_out0, demultiplexer_1_out1, demultiplexer_2_out0, demultiplexer_2_out1,
       demultiplexer_5_out0, demultiplexer_5_out1, demultiplexer_6_out0, demultiplexer_6_out1;
  wire [15:0] multiplexer_1_out, multiplexer_2_out, multiplexer_3_out, multiplexer_4_out, multiplexer_5_out,
       multiplexer_6_out, multiplexer_8_out, multiplexer_9_out;

  Multiplexer #(.width(16), .enable("false")) multiplexer_1 (
    .in0(in_1), .in1(in_2), .out(multiplexer_1_out), .sel(in_8));
  Multiplexer #(.width(16), .enable("false")) multiplexer_2 (
    .in0(in_4), .in1(in_7), .out(multiplexer_2_out), .sel(in_8));
  Multiplexer #(.width(16), .enable("false")) multiplexer_3 (
    .in0(in_11), .in1(in_12), .out(multiplexer_3_out), .sel(in_22));
  Multiplexer #(.width(16), .enable("false")) multiplexer_4 (
    .in0(in_15), .in1(in_17), .out(multiplexer_4_out), .sel(in_22));
  Multiplexer #(.width(16), .enable("false")) multiplexer_5 (
    .in0(in_18), .in1(in_19), .out(multiplexer_5_out), .sel(in_22));
  Multiplexer #(.width(16), .enable("false")) multiplexer_6 (
    .in0(in_20), .in1(in_21), .out(multiplexer_6_out), .sel(in_22));
  Multiplexer #(.width(16), .enable("false")) multiplexer_7 (
    .in0(multiplexer_1_out), .in1(multiplexer_2_out), .out(out_27), .sel(in_9));
  Multiplexer #(.width(16), .enable("false")) multiplexer_8 (
    .in0(multiplexer_3_out), .in1(multiplexer_4_out), .out(multiplexer_8_out), .sel(in_23));
  Multiplexer #(.width(16), .enable("false")) multiplexer_9 (
    .in0(multiplexer_5_out), .in1(multiplexer_6_out), .out(multiplexer_9_out), .sel(in_23));
  Multiplexer #(.width(16), .enable("false")) multiplexer_10 (
    .in0(multiplexer_8_out), .in1(multiplexer_9_out), .out(out_38), .sel(in_24));
  Demultiplexer #(.enable("false")) demultiplexer_1 (
    .out0(demultiplexer_1_out0), .out1(demultiplexer_1_out1), .in(in_3), .sel(in_5));
  Demultiplexer #(.enable("false")) demultiplexer_2 (
    .out0(demultiplexer_2_out0), .out1(demultiplexer_2_out1), .in(in_10), .sel(in_13));
  Demultiplexer #(.enable("false")) demultiplexer_3 (
    .out0(out_25), .out1(out_26), .in(demultiplexer_1_out0), .sel(in_6));
  Demultiplexer #(.enable("false")) demultiplexer_4 (
    .out0(out_28), .out1(out_29), .in(demultiplexer_1_out1), .sel(in_6));
  Demultiplexer #(.enable("false")) demultiplexer_5 (
    .out0(demultiplexer_5_out0), .out1(demultiplexer_5_out1), .in(demultiplexer_2_out0), .sel(in_14));
  Demultiplexer #(.enable("false")) demultiplexer_6 (
    .out0(demultiplexer_6_out0), .out1(demultiplexer_6_out1), .in(demultiplexer_2_out1), .sel(in_14));
  Demultiplexer #(.enable("false")) demultiplexer_7 (
    .out0(out_30), .out1(out_31), .in(demultiplexer_5_out0), .sel(in_16));
  Demultiplexer #(.enable("false")) demultiplexer_8 (
    .out0(out_32), .out1(out_33), .in(demultiplexer_5_out1), .sel(in_16));
  Demultiplexer #(.enable("false")) demultiplexer_9 (
    .out0(out_34), .out1(out_35), .in(demultiplexer_6_out0), .sel(in_16));
  Demultiplexer #(.enable("false")) demultiplexer_10 (
    .out0(out_36), .out1(out_37), .in(demultiplexer_6_out1), .sel(in_16));

  // Notes on the sheet:
  //   a
  //   b
  //   c
  //   d
  //   a
  //   b
  //   c
  //   d
  //   e
  //   f
  //   g
  //   h
  //   mux4way16
  //   mux16
  //   mux16
  //   mux8way16
  //   mux16
  //   mux16
  //   mux16
  //   Dmux4way
  //   Dmux8way
endmodule
