// Logisim project MoarCircuits3.circ as structural Verilog: 1 circuit, main circuit main
module main (
  input  b,
  input  a,
  input  c,
  input  b_2,
  input  a_2,
  input  in_6,
  input  in_7,
  input  in_8,
  output sum,
  output carry,
  output sum_2,
  output out_12,
  output out_13,
  output out_14
);

  wire and_2_out, and_3_out, and_4_out, and_5_out, xor_2_out, xor_3_out;

  xor xor_1 (sum, b, a);
  and and_1 (carry, b, a);
  xor xor_2 (xor_2_out, b_2, a_2);
  xor xor_3 (xor_3_out, in_7, in_8);
  xor xor_4 (sum_2, c, xor_2_out);
  and and_2 (and_2_out, xor_2_out, c);
  and and_3 (and_3_out, b_2, a_2);
  and and_4 (and_4_out, in_7, in_8);
  or or_1 (out_12, and_2_out, and_3_out);
  xor xor_5 (out_13, xor_3_out, in_6);
  and and_5 (and_5_out, xor_3_out, in_6);
  or or_2 (out_14, and_5_out, and_4_out);

  // Notes on the sheet:
  //   Adder
  //   tfw
  //   xor1
  //   Full Adder
  //   xor2
  //   and2
  //   and1
endmodule
