// Logisim project MoarCircuits4.circ as structural Verilog: 1 circuit, main circuit main
module main (
  input  nx,
  input  [15:0] in_2,
  input  zx,
  input  no,
  input  ny,
  input  [15:0] in_6,
  input  f,
  input  zy,
  input  [15:0] in_9,
  input  [15:0] in_10,
  input  in_11,
  input  in_12,
  input  in_13,
  input  in_14,
  output [15:0] out_15,
  output [15:0] out_16,
  output [15:0] out_17,
  output [15:0] out_18,
  output [15:0] out_19,
  output ng,
  output zr,
  output [15:0] out_22
);

  wire multiplexer_1_out;
  wire [15:0] adder_1_out, adder_2_out, adder_3_out, adder_4_out, and_1_out, and_2_out, multiplexer_2_out,
       multiplexer_3_out, not_1_out, not_2_out, not_3_out, not_4_out, not_5_out, not_6_out;

  Multiplexer #(.enable("false")) multiplexer_1 (.in0(in_12), .in1(in_13), .out(multiplexer_1_out), .sel(in_14));
  assign not_1_out = ~in_2;  // NOT_Gate not_1, 16 bits wide
  assign not_2_out = ~in_6;  // NOT_Gate not_2, 16 bits wide
  assign not_3_out = ~in_2;  // NOT_Gate not_3, 16 bits wide
  Adder #(.width(16)) adder_1 (.a(in_2), .b(not_1_out), .out(adder_1_out));  // open: cin, cout
  assign not_4_out = ~in_6;  // NOT_Gate not_4, 16 bits wide
  Adder #(.width(16)) adder_2 (.a(in_6), .b(not_2_out), .out(adder_2_out));  // open: cin, cout
  Multiplexer #(.width(16), .enable("false")) multiplexer_2 (
    .in0(in_2), .in1(not_3_out), .out(multiplexer_2_out), .sel(nx));
  assign not_5_out = ~adder_1_out;  // NOT_Gate not_5, 16 bits wide
  Multiplexer #(.width(16), .enable("false")) multiplexer_3 (
    .in0(in_6), .in1(not_4_out), .out(multiplexer_3_out), .sel(ny));
  assign not_6_out = ~adder_2_out;  // NOT_Gate not_6, 16 bits wide
  assign and_1_out = in_10 & in_9;  // AND_Gate and_1, 16 bits wide
  Multiplexer #(.width(16), .enable("false")) multiplexer_4 (
    .in0(multiplexer_2_out), .in1(not_5_out), .out(out_16), .sel(zx));
  Multiplexer #(.width(16), .enable("false")) multiplexer_5 (
    .in0(multiplexer_3_out), .in1(not_6_out), .out(out_19), .sel(zy));
  Adder #(.width(16)) adder_3 (.a(in_9), .b(in_10), .out(adder_3_out));  // open: cin, cout
  Multiplexer #(.width(16), .enable("false")) multiplexer_6 (
    .in0(and_1_out), .in1(adder_3_out), .out(out_22), .sel(in_11));
  Adder #(.width(16)) adder_4 (.a(out_16), .b(out_19), .out(adder_4_out));  // open: cin, cout
  assign and_2_out = out_19 & out_16;  // AND_Gate and_2, 16 bits wide
  Multiplexer #(.width(16), .enable("false")) multiplexer_7 (.in0(and_2_out), .in1(adder_4_out), .out(out_18), .sel(f));
  Adder #(.width(16)) adder_5 (.a(16'h1), .b(out_18), .out(out_15));  // open: cin, cout
  not not_7 (zr, out_17[0]);
  Multiplexer #(.width(16), .enable("false")) multiplexer_8 (
    .in0(out_18), .in1(out_15), .out({ng, out_17[14:0]}), .sel(no));

  assign out_17[15] = ng;

  // Notes on the sheet:
  //   x
  //   y
endmodule
