// Logisim project PC.circ as structural Verilog: 1 circuit, main circuit main
module main (
  input  le_clock,
  input  [15:0] in_2,
  input  reset,
  input  inc,
  input  in_5,
  input  le_clock_2,
  input  [15:0] in_7,
  input  inc_2,
  input  load,
  input  reset_2,
  input  in_11,
  input  in_12,
  input  in_13,
  output [15:0] out_14,
  output [15:0] out_15,
  output out_16
);

  wire multiplexer_1_out;
  wire [15:0] adder_1_out, adder_2_out, adder_3_out, adder_4_out, multiplexer_2_out, multiplexer_3_out,
       multiplexer_4_out, multiplexer_5_out, multiplexer_6_out, multiplexer_7_out, multiplexer_8_out,
       multiplexer_9_out, multiplexer_10_out, not_1_out, not_2_out, not_3_out, not_4_out;

  Multiplexer #(.enable("false")) multiplexer_1 (.in0(out_16), .in1(in_12), .out(multiplexer_1_out), .sel(in_13));
  D_Flip_Flop d_ff_1 (.clk(in_11), .D(multiplexer_1_out), .Q(out_16));  // open: Qn, preset, en, reset
  Multiplexer #(.width(16), .enable("false")) multiplexer_2 (
    .in0(multiplexer_8_out), .in1(in_2), .out(multiplexer_2_out), .sel(in_5));
  assign not_1_out = ~multiplexer_2_out;  // NOT_Gate not_1, 16 bits wide
  Multiplexer #(.width(16), .enable("false")) multiplexer_3 (
    .in0(multiplexer_2_out), .in1(adder_1_out), .out(multiplexer_3_out), .sel(reset));
  Adder #(.width(16)) adder_1 (.a(multiplexer_2_out), .b(not_1_out), .out(adder_1_out));  // open: cin, cout
  assign not_2_out = ~multiplexer_3_out;  // NOT_Gate not_2, 16 bits wide
  Multiplexer #(.width(16), .enable("false")) multiplexer_4 (
    .in0(multiplexer_3_out), .in1(not_2_out), .out(multiplexer_4_out), .sel(reset));
  Multiplexer #(.width(16), .enable("false")) multiplexer_5 (
    .in0(multiplexer_10_out), .in1(in_7), .out(multiplexer_5_out), .sel(load));
  assign not_3_out = ~multiplexer_5_out;  // NOT_Gate not_3, 16 bits wide
  Adder #(.width(16)) adder_2 (.a(16'h1), .b(out_14), .out(adder_2_out));  // open: cin, cout
  Adder #(.width(16)) adder_3 (.a(multiplexer_5_out), .b(not_3_out), .out(adder_3_out));  // open: cin, cout
  Register #(.width(16)) register_1 (.D(multiplexer_4_out), .Q(out_14), .clk(le_clock));  // open: en, clr
  Multiplexer #(.width(16), .enable("false")) multiplexer_6 (
    .in0(out_14), .in1(adder_2_out), .out(multiplexer_6_out), .sel(inc));
  Multiplexer #(.width(16), .enable("false")) multiplexer_7 (
    .in0(multiplexer_5_out), .in1(adder_3_out), .out(multiplexer_7_out), .sel(reset_2));
  Multiplexer #(.width(16), .enable("false")) multiplexer_8 (
    .in0(multiplexer_6_out), .in1(out_14), .out(multiplexer_8_out), .sel(in_5));
  assign not_4_out = ~multiplexer_7_out;  // NOT_Gate not_4, 16 bits wide
  Multiplexer #(.width(16), .enable("false")) multiplexer_9 (
    .in0(multiplexer_7_out), .in1(not_4_out), .out(multiplexer_9_out), .sel(reset_2));
  Register #(.width(16)) register_2 (.D(multiplexer_9_out), .Q(out_15), .clk(le_clock_2));  // open: en, clr
  Adder #(.width(16)) adder_4 (.a(16'h1), .b(out_15), .out(adder_4_out));  // open: cin, cout
  Multiplexer #(.width(16), .enable("false")) multiplexer_10 (
    .in0(out_15), .in1(adder_4_out), .out(multiplexer_10_out), .sel(inc_2));

  // Notes on the sheet:
  //   Bit
  //   load
endmodule
