// Logisim project Ram64.circ as structural Verilog: 1 circuit, main circuit main
module main (
  input  [15:0] in_1,
  input  clock,
  input  load,
  input  [5:0] in_4,
  output [15:0] out_5
);

  wire demultiplexer_1_out0, demultiplexer_1_out1, demultiplexer_1_out2, demultiplexer_1_out3,
       demultiplexer_1_out4, demultiplexer_1_out5, demultiplexer_1_out6, demultiplexer_1_out7;
  wire [15:0] ram_1_data, ram_2_data, ram_3_data, ram_4_data, ram_5_data, ram_6_data, ram_7_data, ram_8_data;

  RAM #(.addrWidth(3), .dataWidth(16), .bus("separate")) ram_1 (
    .addr(in_4[5:3]), .din(in_1), .data(ram_1_data), .clk(clock), .ld(demultiplexer_1_out0));  // open: str, sel, clr
  RAM #(.addrWidth(3), .dataWidth(16), .bus("separate")) ram_2 (
    .addr(in_4[5:3]), .din(in_1), .data(ram_2_data), .clk(clock), .ld(demultiplexer_1_out1));  // open: str, sel, clr
  RAM #(.addrWidth(3), .dataWidth(16), .bus("separate")) ram_3 (
    .addr(in_4[5:3]), .din(in_1), .data(ram_3_data), .clk(clock), .ld(demultiplexer_1_out2));  // open: str, sel, clr
  RAM #(.addrWidth(3), .dataWidth(16), .bus("separate")) ram_4 (
    .addr(in_4[5:3]), .din(in_1), .data(ram_4_data), .clk(clock), .ld(demultiplexer_1_out3));  // open: str, sel, clr
  RAM #(.addrWidth(3), .dataWidth(16), .bus("separate")) ram_5 (
    .addr(in_4[5:3]), .din(in_1), .data(ram_5_data), .clk(clock), .ld(demultiplexer_1_out4));  // open: str, sel, clr
  RAM #(.addrWidth(3), .dataWidth(16), .bus("separate")) ram_6 (
    .addr(in_4[5:3]), .din(in_1), .data(ram_6_data), .clk(clock), .ld(demultiplexer_1_out5));  // open: str, sel, clr
  RAM #(.addrWidth(3), .dataWidth(16), .bus("separate")) ram_7 (
    .addr(in_4[5:3]), .din(in_1), .data(ram_7_data), .clk(clock), .ld(demultiplexer_1_out6));  // open: str, sel, clr
  RAM #(.addrWidth(3), .dataWidth(16), .bus("separate")) ram_8 (
    .addr(in_4[5:3]), .din(in_1), .data(ram_8_data), .clk(clock), .ld(demultiplexer_1_out7));  // open: str, sel, clr
  Demultiplexer #(.select(3), .enable("false")) demultiplexer_1 (
    .out0(demultiplexer_1_out0), .out1(demultiplexer_1_out1), .out2(demultiplexer_1_out2),
    .out3(demultiplexer_1_out3), .out4(demultiplexer_1_out4), .out5(demultiplexer_1_out5),
    .out6(demultiplexer_1_out6), .out7(demultiplexer_1_out7), .in(load), .sel(in_4[2:0]));
  Multiplexer #(.select(3), .width(16), .enable("false")) multiplexer_1 (
    .in0(ram_1_data), .in1(ram_2_data), .in2(ram_3_data), .in3(ram_4_data), .in4(ram_5_data),
    .in5(ram_6_data), .in6(ram_7_data), .in7(ram_8_data), .out(out_5), .sel(in_4[2:0]));
endmodule
