// Logisim project Some Shitty Invention.circ as structural Verilog: 1 circuit, main circuit main
module main (
  input  [15:0] in_1,
  output [15:0] out_2
);

  wire clock_1_out, keyboard_1_avail;
  wire [6:0] bit_extender_2_out, keyboard_1_data;
  wire [15:0] bit_extender_1_out;

  Clock clock_1 (.out(clock_1_out));
  Keyboard keyboard_1 (.clk(clock_1_out), .avail(keyboard_1_avail), .data(keyboard_1_data));  // open: re, clr
  assign bit_extender_1_out = {{9{1'b0}}, keyboard_1_data};  // Bit_Extender bit_extender_1
  RAM #(.addrWidth(16), .dataWidth(16), .bus("separate")) ram_1 (
    .addr(in_1), .din(bit_extender_1_out), .data(out_2), .str(keyboard_1_avail), .clk(clock_1_out));  // open: sel, ld, clr
  Bit_Extender #(.in_width(16), .out_width(7)) bit_extender_2 (.in(out_2), .out(bit_extender_2_out));
  Hex_Digit_Display hex_digit_display_1 ();  // open: value, dp
  TTY #(.rows(2)) tty_1 (.data(bit_extender_2_out), .clk(clock_1_out));  // open: we, clr
endmodule
